# Fritzing sketch thermoface (saved by Fritzing 0.9.3b)
breadboards: 1

parts:
  Part1 = Arduino Uno (Rev3)
  Part2 = Bluetooth HC-05 Macho
  U1 = LM2596 step down module  # not connected
  M1 = MAX30102  # not connected
  Part3 = Adafruit AMG8833 [part_number="Adafruit #3538"]
  Part4 = Arduino Uno (Rev3)
  Part5 = Adafruit AMG8833 [part_number="Adafruit #3538"]
  Part6 = Arduino Uno (Rev3)
  Part7 = Bluetooth HC-05 Macho

nets:
  N1: Part1.A4/SDA, Part1.A5/SCL, Part3.SDA, Part3.SCL
  N2: Part1.D0/RX, Part2.RXD
  N3: Part1.D1/TX, Part2.TXD
  VCC: Part1.3V3, Part2.VCC, Part3.VCC
  GND: Part1.GND, Part2.GND, Part3.GND
  N4: Part4.A4/SDA, Part5.SDA
  N5: Part4.A5/SCL, Part5.SCL
  5V: Part4.5V, Part5.VCC
  GND_2: Part4.GND, Part5.GND
  N6: Part6.D0/RX, Part7.RXD
  N7: Part6.D1/TX, Part7.TXD
  5V_2: Part6.5V, Part7.VCC
  GND_3: Part6.GND, Part7.GND

custom parts:
  LM2596 step down module: LM2596 DC-DC step down power supply module 3 A.
  MAX30102: Oximeter module using the MAX30102 chip. You may wish to read (and check your module) this post on power problems with these modules: https://reedpaper.wordpress.com/2018/08/22/pulse-oximeter-max30100-max30102-how-to-fix-wrong-board/ . As usual, if you want the mounting holes in pcb, you need to drag a hole over the pad in silkscreen to actually drill the hole (by default they are not drilled)
  Adafruit AMG8833: Add heat-vision to your project and with an Adafruit AMG8833 Grid-EYE Breakout! This sensor from Panasonic is an 8x8 array of IR thermal sensors. When connected to your microcontroller (or raspberry Pi) it will return an array of 64 individual infrared temperature readings over I2C. It's like those fancy thermal cameras, but compact and simple enough for easy integration. This part will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
